# Fritzing sketch Circuit (saved by Fritzing 0.9.9b)
breadboards: 1

parts:
  Mod1 = Raspberry Pi Pico
  BTN_Keyboard = Pushbutton [package="[THT]"]
  BTN_Mouse = Pushbutton [package="[THT]"]
  BTN-Mouse-Button = Pushbutton [package="[THT]"]
  BTN_Speed-Up = Pushbutton [package="[THT]"]
  BTN_Speed-Down = Pushbutton [package="[THT]"]
  LED1 = LED - 3mm [color="Yellow (595nm)" current=0.01 package="3 mm [THT]"]
  LED2 = LED - 3mm [color="Yellow (595nm)" current=0.01 package="3 mm [THT]"]
  LED3 = LED - 3mm [color="Yellow (595nm)" current=0.01 package="3 mm [THT]"]
  R1 = Resistor [tolerance=±1% power=0.25 resistance=100 package=THT]
  R2 = Resistor [tolerance=±1% power=0.25 resistance=100 package=THT]
  R3 = Resistor [tolerance=±1% power=0.25 resistance=100 package=THT]

nets:
  N1: Mod1.pin_3, Mod1.pin_8, Mod1.pin_13, Mod1.pin_18, Mod1.pin_23, Mod1.pin_28, Mod1.pin_33, Mod1.pin_38, Mod1.pin_42, BTN_Keyboard.Pin_3, BTN_Keyboard.Pin_4, BTN_Mouse.Pin_1, BTN_Mouse.Pin_2, BTN-Mouse-Button.Pin_3, BTN-Mouse-Button.Pin_4, BTN_Speed-Up.Pin_1, BTN_Speed-Up.Pin_2, BTN_Speed-Down.Pin_3, BTN_Speed-Down.Pin_4, LED1.cathode, LED2.cathode
  N2: Mod1.pin_21, BTN_Speed-Down.Pin_1, BTN_Speed-Down.Pin_2
  N3: Mod1.pin_22, BTN_Speed-Up.Pin_3, BTN_Speed-Up.Pin_4
  N4: Mod1.pin_24, BTN-Mouse-Button.Pin_1, BTN-Mouse-Button.Pin_2
  N5: Mod1.pin_25, BTN_Mouse.Pin_3, BTN_Mouse.Pin_4
  N6: Mod1.pin_26, BTN_Keyboard.Pin_1, BTN_Keyboard.Pin_2
  N7: Mod1.pin_29, R3.Pin_1
  N8: Mod1.pin_30, R2.Pin_1
  N9: Mod1.pin_31, R1.Pin_1
  N10: LED1.anode, R3.Pin_0
  N11: LED2.anode, R1.Pin_0
  N12: LED3.anode, R2.Pin_0

notes:
  this image was created with Fritzing

custom parts:
  Raspberry Pi Pico: Raspberry Pi Pico. Based around the RP2040 microcontroller the Pico is a low cost microcontroller device bringing Raspberry Pi quality, cost, and easy of use to the microcontroller space. Jan 2021, Split part in to two versions: tht (this one) and SMD. This one will drill holes for a .1 in header in pcb to allow plugging in the module as well as providing pads to solder the module to the top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
